// Logisim project WH02.circ as structural Verilog: 13 circuits, main circuit main
module main (
);

  wire button_1_out, C_FLAG, CLK, ENABLE_PRGC, EQ_FLAG, GT_FLAG, HLT, LT_FLAG, not_1_out, or_2_out, OUTPUT_A,
       OUTPUT_ACC, OUTPUT_B, OUTPUT_C, OUTPUT_INST, OUTPUT_MEM_ADD, OUTPUT_O1, OUTPUT_O2, OUTPUT_PRGC,
       OUTPUT_RAM, OUTPUT_STACK, PULL, Reset1, RST_STEPCOUNTER, STACK_DEC, STACK_INC, SYS_RST, undriven,
       WRITE_A, WRITE_ACC, WRITE_B, WRITE_C, WRITE_FLAGS, WRITE_INST, WRITE_MEM_ADD, WRITE_O1, WRITE_O2,
       WRITE_PRGC, WRITE_RAM, WRITE_STACK;
  wire [1:0] SCT, SLC;
  wire [2:0] SFT, STEP_BUS;
  wire [3:3] pull_resistor_2_node;
  wire [7:0] A_BUS, ACC_BUS, ALU_BUS, B_BUS, C_BUS, DBUS, FLAG_BUS, INST_BUS, MEM_ADD_BUS, O1_BUS, O2_BUS,
       PRGC_BUS, RAM_BUS, STACK_BUS, STACK_PTR;
  wire [7:4] FLAG_REGISTER_o1;
  wire [31:0] rom_1_data;

  Button button_1 (.out(button_1_out));
  or or_1 (SYS_RST, button_1_out, Reset1);
  Pull_Resistor pull_resistor_1 (.node(PULL));
  Hex_Digit_Display hex_digit_display_1 (.value(DBUS[7:4]));  // open: dp
  EightBitRegister A_Register (
    .RDY(1'b1), .WE(WRITE_A), .RST(SYS_RST), .VCC(1'b1), .CLK(CLK), .DI(DBUS), .OE(OUTPUT_A), .O(DBUS),
    .O1(A_BUS));
  EightBitRegister O1_Register (
    .RDY(1'b1), .WE(WRITE_O1), .RST(SYS_RST), .VCC(1'b1), .CLK(CLK), .DI(DBUS), .OE(OUTPUT_O1), .O1(O1_BUS));  // open: O
  ProgramCounter Program_Counter (
    .OE(OUTPUT_PRGC), .CE(ENABLE_PRGC), .CLK(CLK), .RST(SYS_RST), .WE(WRITE_PRGC), .D(DBUS), .O1(PRGC_BUS),
    .O(DBUS));
  EightBitRegister Instruction_Register (
    .RDY(1'b1), .WE(WRITE_INST), .RST(SYS_RST), .VCC(1'b1), .CLK(CLK), .DI(RAM_BUS), .OE(OUTPUT_INST),
    .O(DBUS), .O1(INST_BUS));
  Hex_Digit_Display hex_digit_display_2 (.value(DBUS[3:0]));  // open: dp
  SystemClock systemclock_1 (.HLT(HLT), .RST(SYS_RST), .O(CLK));
  Hex_Digit_Display hex_digit_display_3 (.value(A_BUS[7:4]));  // open: dp
  or or_2 (or_2_out, SYS_RST, RST_STEPCOUNTER);
  not not_1 (not_1_out, CLK);
  Hex_Digit_Display hex_digit_display_4 (.value(A_BUS[3:0]));  // open: dp
  Hex_Digit_Display hex_digit_display_5 (.value(B_BUS[7:4]));  // open: dp
  EightBitRegister B_Register (
    .RDY(1'b1), .WE(WRITE_B), .RST(SYS_RST), .VCC(1'b1), .CLK(CLK), .DI(DBUS), .OE(OUTPUT_B), .O(DBUS),
    .O1(B_BUS));
  EightBitRegister O2_Register (
    .RDY(1'b1), .WE(WRITE_O2), .RST(SYS_RST), .VCC(1'b1), .CLK(CLK), .DI(DBUS), .OE(OUTPUT_O2), .O1(O2_BUS));  // open: O
  StepCounter Step_Counter (.RST(or_2_out), .CLK(not_1_out), .O(STEP_BUS));
  Hex_Digit_Display hex_digit_display_6 (.value(B_BUS[3:0]));  // open: dp
  Hex_Digit_Display hex_digit_display_7 (.value(C_BUS[7:4]));  // open: dp
  EightBitRegister Memory_Address_Register (
    .RDY(1'b1), .WE(WRITE_MEM_ADD), .RST(SYS_RST), .VCC(1'b1), .CLK(CLK), .DI(DBUS), .OE(OUTPUT_MEM_ADD),
    .O(DBUS), .O1(MEM_ADD_BUS));
  Hex_Digit_Display hex_digit_display_8 (.value(C_BUS[3:0]));  // open: dp
  Hex_Digit_Display hex_digit_display_9 (.value(ACC_BUS[7:4]));  // open: dp
  Hex_Digit_Display hex_digit_display_10 (.value(ACC_BUS[3:0]));  // open: dp
  Button button_2 (.out(Reset1));
  Hex_Digit_Display hex_digit_display_11 (.value(ALU_BUS[7:4]));  // open: dp
  Hex_Digit_Display hex_digit_display_12 (.value(ALU_BUS[3:0]));  // open: dp
  EightBitRegister C_Register (
    .RDY(1'b1), .WE(WRITE_C), .RST(SYS_RST), .VCC(1'b1), .CLK(CLK), .DI(DBUS), .OE(OUTPUT_C), .O(DBUS),
    .O1(C_BUS));
  ArithmeticLogicUnit ALU (
    .SFT(SFT), .RDY(1'b1), .VCC(1'b1), .SCT(SCT), .D1(A_BUS), .D2(B_BUS), .O1(ALU_BUS), .C(FLAG_BUS[3]),
    .GT(FLAG_BUS[0]), .EQ(FLAG_BUS[1]), .LT(FLAG_BUS[2]));  // open: OE, O
  RamUnit RAM (.ADR(MEM_ADD_BUS), .WE(WRITE_RAM), .CLK(CLK), .D(DBUS), .OE(OUTPUT_RAM), .O1(RAM_BUS), .O(DBUS));
  Hex_Digit_Display hex_digit_display_13 (.value(O1_BUS[3:0]));  // open: dp
  Hex_Digit_Display hex_digit_display_14 (.value(O1_BUS[7:4]));  // open: dp
  ROM #(.addrWidth(11), .dataWidth(32)) rom_1 (
    .addr({STEP_BUS, INST_BUS}),
    .data({rom_1_data[31:20], STACK_DEC, STACK_INC, RST_STEPCOUNTER, HLT, SFT, SLC, ENABLE_PRGC, rom_1_data[9:0]}));
  Hex_Digit_Display hex_digit_display_15 (.value(O2_BUS[7:4]));  // open: dp
  Hex_Digit_Display hex_digit_display_16 (.value(O2_BUS[3:0]));  // open: dp
  Hex_Digit_Display hex_digit_display_17 (.value(PRGC_BUS[7:4]));  // open: dp
  Hex_Digit_Display hex_digit_display_18 (.value(PRGC_BUS[3:0]));  // open: dp
  Hex_Digit_Display hex_digit_display_19 (.value(INST_BUS[7:4]));  // open: dp
  EightBitRegister Accumulator (
    .RDY(1'b1), .WE(WRITE_ACC), .RST(SYS_RST), .VCC(1'b1), .CLK(CLK), .DI(ALU_BUS), .OE(OUTPUT_ACC),
    .O(DBUS), .O1(ACC_BUS));
  EightBitRegister FLAG_REGISTER (
    .RDY(1'b1), .WE(WRITE_FLAGS), .RST(SYS_RST), .VCC(1'b1), .CLK(CLK), .DI(FLAG_BUS), .OE(undriven),
    .O1({FLAG_REGISTER_o1, C_FLAG, LT_FLAG, EQ_FLAG, GT_FLAG}));  // open: O
  Hex_Digit_Display hex_digit_display_20 (.value(INST_BUS[3:0]));  // open: dp
  Hex_Digit_Display hex_digit_display_21 (.value({pull_resistor_2_node[3], STEP_BUS}));  // open: dp
  Hex_Digit_Display hex_digit_display_22 (.value(MEM_ADD_BUS[7:4]));  // open: dp
  Hex_Digit_Display hex_digit_display_23 (.value(MEM_ADD_BUS[3:0]));  // open: dp
  Pull_Resistor pull_resistor_2 (.node(pull_resistor_2_node[3]));
  Decoder #(.select(4)) decoder_1 (
    .out0(OUTPUT_A), .out1(OUTPUT_B), .out2(OUTPUT_C), .out3(OUTPUT_ACC), .out4(OUTPUT_O1), .out5(OUTPUT_O2),
    .out6(OUTPUT_PRGC), .out7(OUTPUT_MEM_ADD), .out8(OUTPUT_INST), .out9(OUTPUT_RAM), .out10(OUTPUT_STACK),
    .sel(rom_1_data[3:0]), .en(rom_1_data[8]));  // open: out11, out12, out13, out14, out15
  Decoder #(.select(4)) decoder_2 (
    .out0(WRITE_A), .out1(WRITE_B), .out2(WRITE_C), .out3(WRITE_O1), .out4(WRITE_O2), .out5(WRITE_FLAGS),
    .out6(WRITE_PRGC), .out7(WRITE_MEM_ADD), .out8(WRITE_INST), .out9(WRITE_RAM), .out10(WRITE_STACK),
    .out11(WRITE_ACC), .sel(rom_1_data[7:4]), .en(rom_1_data[9]));  // open: out12, out13, out14, out15
  Hex_Digit_Display hex_digit_display_24 (.value(RAM_BUS[7:4]));  // open: dp
  Hex_Digit_Display hex_digit_display_25 (.value(RAM_BUS[3:0]));  // open: dp
  Hex_Digit_Display hex_digit_display_26 (.value(STACK_BUS[7:4]));  // open: dp
  Hex_Digit_Display hex_digit_display_27 (.value(STACK_BUS[3:0]));  // open: dp
  Stack stack_1 (
    .CLK(CLK), .SI(STACK_INC), .SD(STACK_DEC), .D(DBUS), .WE(WRITE_STACK), .OE(OUTPUT_STACK), .RST(SYS_RST),
    .SP(STACK_PTR), .O1(STACK_BUS), .O(DBUS));

  // Notes on the sheet:
  //   contents of rom_1 (hex, n*v repeats v):
  //   256*376 256*789 0 310 320 330 340 398 301 321 331 341 398 302 312 332 342 398 304 314 324 344 398
  //   305 315 325 335 398 6*379 10000 6*376 303 313 323 333 343 376 213*0 20000 20000 20000 390 2b0 20000
  //   20000 20000 391 2b0 2b0 20000 20000 392 2b0 2b0 20000 20000 394 2b0 2b0 20000 20000 395 309 319 329
  //   339 349 7a9 0 709 719 729 739 749 7a9 0 0 20000 20000 20000 7a9 212*0 2b0 0 0 0 20000 20000 0 0 0
  //   20000 20000 20000 0 0 20000 20000 20000 0 0 0 20000 20000 0 0 20000 2b0 2b0 20000 20000 20000 376 0
  //   2b0 2b0 20000 20000 20000 376 2b0 2b0 0 0 0 376 212*0 20000 24*0 20000 20000 0 0 0 79a 0 20000 20000
  //   0 0 0 79a 20000 20000 0 0 0 79a 242*0 20000 12*0 20000
  //   INST
  //   STEP
endmodule

module EightBitRegister (
  input  OE,
  input  WE,
  input  RST,
  input  VCC,
  input  CLK,
  input  [7:0] DI,
  input  RDY,
  output [7:0] O1,
  output [7:0] O
);

  wire button_1_out, button_2_out, CLK_t, D1, D2, D3, D4, D5, D6, D7, D8, multiplexedswitch_2_o, or_3_out,
       pull_resistor_4_node, R, switch_1_p2, switch_2_p2, switch_4_p2, switch_5_p2, W, WE_t;
  wire [7:0] eightbitbufferedinput_1_o, undriven;

  // Switch switch_1: pin names not known; wires that end beside it: VCC, switch_1_p2
  // Switch switch_2: pin names not known; wires that end beside it: VCC, switch_2_p2
  Button button_1 (.out(button_1_out));
  Button button_2 (.out(button_2_out));
  // DipSwitch dipswitch_1: pin names not known
  Pull_Resistor pull_resistor_1 (.node(W));
  and and_1 (W, WE_t, CLK_t);
  MultiplexedSwitch multiplexedswitch_1 (.D1(WE), .D2(switch_1_p2), .STC(switch_2_p2), .RDY(RDY), .O(WE_t));
  Pull_Resistor pull_resistor_2 (.node(R));
  or or_1 (R, RST, button_1_out);
  Pull_Resistor pull_resistor_3 (.node(CLK_t));
  or or_2 (CLK_t, CLK, button_2_out);
  Multiplexer #(.width(8)) multiplexer_1 (
    .in0(undriven), .in1(eightbitbufferedinput_1_o), .out({D8, D7, D6, D5, D4, D3, D2, D1}), .sel(or_3_out));
  EightBitBufferedInput eightbitbufferedinput_1 (.D(DI), .E(WE_t), .O(eightbitbufferedinput_1_o));
  or or_3 (or_3_out, pull_resistor_4_node, RDY);
  Pull_Resistor pull_resistor_4 (.node(pull_resistor_4_node));
  // Switch switch_3: pin names not known; wires that end beside it: VCC, pull_resistor_4_node
  Pull_Resistor pull_resistor_5 (.node(RDY));
  assign O = multiplexedswitch_2_o ? O1 : 8'bz;  // Controlled_Buffer controlled_buffer_1
  // Switch switch_4: pin names not known; wires that end beside it: VCC, switch_4_p2
  // Switch switch_5: pin names not known; wires that end beside it: VCC, switch_5_p2
  MultiplexedSwitch multiplexedswitch_2 (
    .D1(OE), .D2(switch_4_p2), .STC(switch_5_p2), .RDY(RDY), .O(multiplexedswitch_2_o));
  Pull_Resistor pull_resistor_6 (.node(D1));
  Pull_Resistor pull_resistor_7 (.node(D2));
  Pull_Resistor pull_resistor_8 (.node(D3));
  Pull_Resistor pull_resistor_9 (.node(D4));
  Pull_Resistor pull_resistor_10 (.node(D5));
  Pull_Resistor pull_resistor_11 (.node(D6));
  Pull_Resistor pull_resistor_12 (.node(D7));
  Pull_Resistor pull_resistor_13 (.node(D8));
  D_Flip_Flop d_ff_1 (.D(D1), .clk(W), .Q(O1[0]), .reset(R));  // open: Qn, preset
  D_Flip_Flop d_ff_2 (.D(D2), .clk(W), .Q(O1[1]), .reset(R));  // open: Qn, preset
  D_Flip_Flop d_ff_3 (.D(D3), .clk(W), .Q(O1[2]), .reset(R));  // open: Qn, preset
  D_Flip_Flop d_ff_4 (.D(D4), .clk(W), .Q(O1[3]), .reset(R));  // open: Qn, preset
  D_Flip_Flop d_ff_5 (.D(D5), .clk(W), .Q(O1[4]), .reset(R));  // open: Qn, preset
  D_Flip_Flop d_ff_6 (.D(D6), .clk(W), .Q(O1[5]), .reset(R));  // open: Qn, preset
  D_Flip_Flop d_ff_7 (.D(D7), .clk(W), .Q(O1[6]), .reset(R));  // open: Qn, preset
  D_Flip_Flop d_ff_8 (.D(D8), .clk(W), .Q(O1[7]), .reset(R));  // open: Qn, preset

  // Other names for the same wires on the sheet: O1_t = O1[0]; O2 = O1[1]; O3 = O1[2]; O4 = O1[3]; O5 = O1[4];
  //   O6 = O1[5]; O7 = O1[6]; O8 = O1[7]
endmodule

module MultiplexedSwitch (
  input  D1,
  input  D2,
  input  STC,
  input  RDY,
  output O
);

  wire not_1_out, not_2_out, or_1_out;

  Pull_Resistor pull_resistor_1 (.node(D1));
  Pull_Resistor pull_resistor_2 (.node(D2));
  not not_1 (not_1_out, or_1_out);
  or or_1 (or_1_out, not_2_out, RDY);
  not not_2 (not_2_out, STC);
  Pull_Resistor pull_resistor_3 (.node(STC));
  Pull_Resistor pull_resistor_4 (.node(O));
  Multiplexer multiplexer_1 (.in0(D1), .in1(D2), .out(O), .sel(not_1_out));
  Pull_Resistor pull_resistor_5 (.node(RDY));
endmodule

module SystemClock (
  input  HLT,
  input  RST,
  output O
);

  wire clock_1_out, d_ff_1_q, not_1_out;

  Pull_Resistor pull_resistor_1 (.node(HLT));
  Pull_Resistor pull_resistor_2 (.node(RST));
  D_Flip_Flop d_ff_1 (.D(HLT), .clk(HLT), .Q(d_ff_1_q), .reset(RST));  // open: Qn, preset
  Clock clock_1 (.out(clock_1_out));
  not not_1 (not_1_out, d_ff_1_q);
  Pull_Resistor pull_resistor_3 (.node(O));
  assign O = not_1_out ? clock_1_out : 1'bz;  // Controlled_Buffer controlled_buffer_1
endmodule

module ArithmeticLogicUnit (
  input  [1:0] SCT,
  input  [2:0] SFT,
  input  RDY,
  input  VCC,
  input  [7:0] D1,
  input  [7:0] D2,
  input  OE,
  output GT,
  output EQ,
  output LT,
  output [7:0] O,
  output [7:0] O1,
  output C
);

  wire ADD_C_OUT, multiplexer_2_out, OE_t, SUB_C_OUT, switch_1_p2, switch_2_p2;
  wire [7:0] ADD_OUT, LSFT_OUT, RSFT_OUT, SUB_OUT;

  // Switch switch_1: pin names not known; wires that end beside it: VCC, switch_1_p2
  // Switch switch_2: pin names not known; wires that end beside it: VCC, switch_2_p2
  MultiplexedSwitch multiplexedswitch_1 (.D1(OE), .D2(switch_1_p2), .STC(switch_2_p2), .RDY(RDY), .O(OE_t));
  Multiplexer #(.select(2), .width(8)) multiplexer_1 (
    .in0(ADD_OUT), .in1(SUB_OUT), .in2(LSFT_OUT), .in3(RSFT_OUT), .out(O1), .sel(SCT));
  Multiplexer multiplexer_2 (.in0(ADD_C_OUT), .in1(SUB_C_OUT), .out(multiplexer_2_out), .sel(SCT[1]));
  assign O = OE_t ? O1 : 8'bz;  // Controlled_Buffer controlled_buffer_1
  Pull_Resistor pull_resistor_1 (.node(C));
  assign C = OE_t ? multiplexer_2_out : 1'bz;  // Controlled_Buffer controlled_buffer_2
  Adder adder_1 (.a(D1), .b(D2), .out(ADD_OUT), .cout(ADD_C_OUT));  // open: cin
  Subtractor subtractor_1 (.a(D1), .b(D2), .out(SUB_OUT), .bout(SUB_C_OUT));  // open: bin
  Comparator comparator_1 (.a(D1), .b(D2), .gt(GT), .eq(EQ), .lt(LT));
  Shifter shifter_1 (.in(D1), .\dist (SFT), .out(LSFT_OUT));
  Shifter #(.shift("lr")) shifter_2 (.in(D1), .\dist (SFT), .out(RSFT_OUT));
  Pull_Resistor pull_resistor_2 (.node(GT));
  Pull_Resistor pull_resistor_3 (.node(EQ));
  Pull_Resistor pull_resistor_4 (.node(LT));
endmodule

module ProgramCounter (
  input  OE,
  input  CE,
  input  CLK,
  input  RST,
  input  WE,
  input  [7:0] D,
  output [7:0] O1,
  output [7:0] O
);

  Counter counter_1 (.clr(RST), .load(WE), .count(CE), .clk(CLK), .D(D), .Q(O1));  // open: up, carry
  assign O = OE ? O1 : 8'bz;  // Controlled_Buffer controlled_buffer_1

  // Other names for the same wires on the sheet: COUNT_ENABLE = CE; WRITE = WE
endmodule

module StepCounter (
  input  RST,
  input  CLK,
  output [2:0] O
);

  wire not_1_out;

  not not_1 (not_1_out, CLK);
  Counter #(.max('h7), .width(3)) Step_Counter (
    .clr(RST), .count(not_1_out), .clk(not_1_out), .Q(O));  // open: load, up, D, carry
endmodule

module RamUnit (
  input  [7:0] ADR,
  input  WE,
  input  CLK,
  input  [7:0] D,
  input  OE,
  output [7:0] O1,
  output [7:0] O
);

  wire not_1_out, not_2_out;
  wire [7:0] eightbitbufferedinput_1_o;

  RAM ram_1 (.addr(ADR), .we(WE), .oe(not_1_out), .clk(not_2_out), .din(eightbitbufferedinput_1_o), .dout(O1));
  not not_1 (not_1_out, WE);
  not not_2 (not_2_out, CLK);
  EightBitBufferedInput eightbitbufferedinput_1 (.D(D), .E(WE), .O(eightbitbufferedinput_1_o));
  EightBitBufferedInput eightbitbufferedinput_2 (.D(O1), .E(OE), .O(O));
endmodule

module SixteenBitRegister (
  input  [15:0] D,
  input  CLK,
  input  RST,
  input  VCC,
  input  RDY,
  input  OE,
  input  WE,
  output [15:0] O,
  output [15:0] O1
);

  wire [7:0] O1_t, O2;

  EightBitRegister eightbitregister_1 (
    .RDY(RDY), .WE(WE), .RST(RST), .VCC(VCC), .CLK(CLK), .DI(D[7:0]), .OE(OE), .O(O1_t), .O1(O1[7:0]));
  EightBitRegister eightbitregister_2 (
    .RDY(RDY), .WE(WE), .RST(RST), .VCC(VCC), .CLK(CLK), .DI(D[15:8]), .OE(OE), .O(O2), .O1(O1[15:8]));
  assign O = OE ? {O2, O1_t} : 16'bz;  // Controlled_Buffer controlled_buffer_1

  // Other names for the same wires on the sheet: D1[7:0] = D[7:0]; D2[7:0] = D[15:8]; O1_1[7:0] = O1[7:0];
  //   O2_1[7:0] = O1[15:8]
endmodule

module Stack (
  input  OE,
  input  RST,
  input  CLK,
  input  SI,
  input  SD,
  input  [7:0] D,
  input  WE,
  output [7:0] SP,
  output [7:0] O1,
  output [7:0] O
);

  wire pull_resistor_1_node;
  wire [7:0] D_t;

  EightBitBufferedInput eightbitbufferedinput_1 (.D(D), .E(WE), .O(D_t));
  Counter counter_1 (.clr(RST), .up(SI), .count(SD), .clk(CLK), .Q(SP));  // open: load, D, carry
  RAM ram_1 (.addr(SP), .we(WE), .oe(pull_resistor_1_node), .clk(CLK), .din(D_t), .dout(O1));
  Pull_Resistor #(.pull(1)) pull_resistor_1 (.node(pull_resistor_1_node));
  EightBitBufferedInput eightbitbufferedinput_2 (.D(O1), .E(OE), .O(O));

  // Other names for the same wires on the sheet: DEC = SD; INC = SI; Stack_Pointer[7:0] = SP
endmodule

module ThirtyTwoBitRegister (
  input  [31:0] D,
  input  CLK,
  input  RST,
  input  VCC,
  input  RDY,
  input  OE,
  input  WE,
  output [31:0] O,
  output [31:0] O1
);

  wire [7:0] O1_t, O2, O3, O4;

  EightBitRegister eightbitregister_1 (
    .RDY(RDY), .WE(WE), .RST(RST), .VCC(VCC), .CLK(CLK), .DI(D[7:0]), .OE(OE), .O(O1_t), .O1(O1[7:0]));
  EightBitRegister eightbitregister_2 (
    .RDY(RDY), .WE(WE), .RST(RST), .VCC(VCC), .CLK(CLK), .DI(D[15:8]), .OE(OE), .O(O2), .O1(O1[15:8]));
  EightBitRegister eightbitregister_3 (
    .RDY(RDY), .WE(WE), .RST(RST), .VCC(VCC), .CLK(CLK), .DI(D[23:16]), .OE(OE), .O(O3), .O1(O1[23:16]));
  EightBitRegister eightbitregister_4 (
    .RDY(RDY), .WE(WE), .RST(RST), .VCC(VCC), .CLK(CLK), .DI(D[31:24]), .OE(OE), .O(O4), .O1(O1[31:24]));
  assign O = OE ? {O4, O3, O2, O1_t} : 32'bz;  // Controlled_Buffer controlled_buffer_1

  // Other names for the same wires on the sheet: D1[7:0] = D[7:0]; D2[7:0] = D[15:8]; D3[7:0] = D[23:16];
  //   D4[7:0] = D[31:24]; O1_1[7:0] = O1[7:0]; O2_1[7:0] = O1[15:8]; O3_1[7:0] = O1[23:16]; O4_1[7:0] = O1[31:24]
endmodule

module BufferedInput (
  input  D,
  input  E,
  output O
);

  assign O = E ? D : 1'bz;  // Controlled_Buffer controlled_buffer_1
endmodule

module EightBitBufferedInput (
  input  [7:0] D,
  input  E,
  output [7:0] O
);

  assign O = E ? D : 8'bz;  // Controlled_Buffer controlled_buffer_1
endmodule
